# Fritzing sketch sketch (saved by Fritzing 0.9.3b)
circuit board: 8.46667cm x 5.64444cm
breadboards: 1

parts:
  WeMos_D1_Mini1 = WeMos D1 Mini
  Grove1 = Grove OLED 128x96
  S1 = Pushbutton [package="[THT]"]
  R1 = Resistor [tolerance=±5% resistance=10k package=THT]
  Q1 = PNP-Transistor [package="TO92 [THT]"]
  R2 = Resistor [tolerance=±5% resistance=33k package=THT]
  C1 = Electrolytic Capacitor [capacitance=1µF package="100 mil [THT, electrolytic]"]
  D1 = Rectifier Diode [part_number=1N4001 package="300 mil [THT]"]

nets:
  3V3: WeMos_D1_Mini1.3V3, Grove1.VCC, Q1.E
  N1: WeMos_D1_Mini1.D0, WeMos_D1_Mini1.RST, D1.anode
  N2: WeMos_D1_Mini1.D1, Grove1.SCL
  N3: WeMos_D1_Mini1.D2, Grove1.SDA
  N4: WeMos_D1_Mini1.D5, R1.Pin_0, Q1.C
  N5: WeMos_D1_Mini1.G, Grove1.GND, S1.Pin_1, S1.Pin_2, R2.Pin_0, C1.-
  N6: S1.Pin_3, S1.Pin_4, R1.Pin_1, D1.cathode
  N7: Q1.B, R2.Pin_1, C1.+
